# Fritzing sketch touchyfeelylamp (saved by Fritzing 0.6.3b)
breadboards: 1

parts:
  Arduino1 = Arduino
  LCD1 = LCD screen
  J1 = Basic Servo
  J2 = Piezo Speaker
  R1 = Trimmer Potentiometer [maximum_resistance=10kΩ package=THT]
  T1 = LM35 Temperature Sensor [package="TO92 [THT]"]

nets (from the breadboard view):
  GND: Arduino1.GND, LCD1.LED-, J1.gnd, T1.GND
  N1: Arduino1.D12, J1.pulse
  N2: Arduino1.D11, LCD1.DB7
  N3: Arduino1.D10, LCD1.DB6
  N4: Arduino1.D9, LCD1.DB5
  N5: Arduino1.D8, LCD1.DB4
  N6: Arduino1.D7, LCD1.E
  N7: Arduino1.D6, LCD1.RS
  N8: Arduino1.D4, J2.pin2
  +5V: Arduino1.+5V, LCD1.LED+, J1.vcc, T1.+Vs
  N9: Arduino1.A0, T1.Vout
  N10: LCD1.VSS, LCD1.R/W, J2.pin1, R1.leg1
  N11: LCD1.VDD, R1.leg2
  N12: LCD1.V0, R1.wiper

notes:
  BLUETOOTH ADAPTER
