# Fritzing sketch touchyfeelylamp (saved by Fritzing 0.7.10b)
breadboards: 1

parts:
  Arduino1 = Arduino
  LED1 = LED - 5mm [color="Red (635nm)" package="5 mm [THT]"]
  R3 = Resistor [tolerance=±5% resistance=1M package=THT]
  R4 = Resistor [tolerance=±5% resistance=220 package=THT]

nets:
  N1: Arduino1.GND, Arduino1.D12, LED1.anode, R4.Pin_0
  N2: Arduino1.D4, R3.Pin_0
  N3: Arduino1.D2, R3.Pin_1
  N4: LED1.cathode, R4.Pin_1

notes:
  METAL FOIL
